# Fritzing sketch mood_cube (saved by Fritzing 1.0.7)
circuit board: 4.5cm x 4.5cm
circuit board: 4.5cm x 4.5cm
breadboards: 2

parts:
  cubeGrip = Microbit (basic)
  2SC1815_1 = NPN-Transistor [package="TO92 [THT]"]
  D1 = Rectifier Diode [part_number=1N4007 package="300 mil [THT]"]
  R2 = Resistor [tolerance=±5% power=0.25W resistance=220 package=THT]
  cubeTouch = Microbit (basic)
  4_5VDC_2 = Battery [internal_resistance=0.1Ω]
  2SC1815_2 = NPN-Transistor [package="TO92 [THT]"]
  D2 = Rectifier Diode [part_number=1N4007 package="300 mil [THT]"]
  Aluminum-Mesh = Antenna
  VIB2 = DC Motor [voltage_(max)=6V voltage_(min)=3V]
  VIB1 = DC Motor [voltage_(max)=6V voltage_(min)=3V]
  R4 = Basic Force Sensing Resistor (FSR) [package=THT]
  4_5VDC_1 = Battery [internal_resistance=0.1Ω]
  S2 = Toggle Switch [package=THT]
  S1 = Toggle Switch [package=THT]
  PL9823_1 = RGB LED PL9823 F5 [package="5 mm [THT]"]
  PL9823_2 = RGB LED PL9823 F5 [package="5 mm [THT]"]
  C2 = Electrolytic Capacitor [capacitance=100µF voltage=35V package="100 mil [THT, electrolytic]"]
  C3 = Ceramic Capacitor [capacitance=100nF voltage=35V package="100 mil [THT, multilayer]"]
  R3 = Resistor [tolerance=±5% power=0.25W resistance=220 package=THT]
  C4 = Electrolytic Capacitor [capacitance=100µF voltage=35V package="100 mil [THT, electrolytic]"]
  C5 = Ceramic Capacitor [capacitance=100nF voltage=35V package="100 mil [THT, multilayer]"]
  R6 = Resistor [tolerance=±5% power=0.25W resistance=220 package=THT]
  R5 = Resistor [tolerance=±5% power=0.25W resistance=220 package=THT]
  R1 = Resistor [tolerance=±5% power=0.25W resistance=4.7k package=THT]
  C1 = Ceramic Capacitor [capacitance=0.1µF voltage=50V package="100 mil [THT, multilayer]"]
  NJU7043D = IC, DIP package, 8 pins [chip_label=7043D]

nets:
  N1: cubeGrip.P0, NJU7043D.pin1, NJU7043D.pin2
  N2: cubeGrip.P1, R2.Pin_1
  N3: cubeGrip.P2, R3.Pin_0
  N4: cubeGrip.3V3, R1.Pin_0, C1.0, NJU7043D.pin8
  N5: cubeGrip.Bat_-, 2SC1815_1.E, R4.pin_2, 4_5VDC_1.-, PL9823_1.GND, C2.-, C3.0, C1.1, NJU7043D.pin4, NJU7043D.pin5
  N6: cubeGrip.Bat_+, D1.cathode, VIB1.pin_1, 4_5VDC_1.+, S1.L1, S1.COM, PL9823_1.VDD, C2.+, C3.1
  N7: 2SC1815_1.B, R2.Pin_0
  N8: 2SC1815_1.C, D1.anode, VIB1.pin_2
  N9: cubeTouch.P0, Aluminum-Mesh.antenna_lead
  N10: cubeTouch.P1, R5.Pin_1
  N11: cubeTouch.P2, R6.Pin_0
  N12: cubeTouch.Bat_-, 4_5VDC_2.-, 2SC1815_2.E, PL9823_2.GND, C4.-, C5.0
  N13: cubeTouch.Bat_+, 4_5VDC_2.+, D2.cathode, VIB2.pin_1, S2.L1, S2.COM, PL9823_2.VDD, C4.+, C5.1
  N14: 2SC1815_2.B, R5.Pin_0
  N15: 2SC1815_2.C, D2.anode, VIB2.pin_2
  N16: R4.pin_1, R1.Pin_1, NJU7043D.pin3
  N17: PL9823_1.DIN, R3.Pin_1
  N18: PL9823_2.DIN, R6.Pin_1
  N19: NJU7043D.pin6, NJU7043D.pin7

notes:
  cubeGrip
  cubeTouch
  4.5VDC (AAx3)
  MICROBIT_JST
  +-
  +210
  210
  43
  512
  (4)
  (3)
  (5)
  (2)
  (1)
  (6)

custom parts:
  Microbit (basic): BBC Microbit Fritzing part. May 2019 expanded to include schematic and pcb views as well as breadboard. PCB view assumes an Adafruit PRODUCT ID: 3342 2x40 Right Angle through hole edge connector (although others will probably work as well). The pcb svg is custom (see forum article http://forum.fritzing.org/t/making-edge-connectors-and-both-side-smd-parts/7287 for an explaination if you need to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
  RGB LED PL9823 F5: A 5mm tri-color LED with red, green and blue inside. this led includes WS2811 controller.
